# Fritzing sketch smartPJUSchema (saved by Fritzing 0.9.6b)
breadboards: 1

parts:
  Part1 = Arduino Uno (Rev3) - ICSP
  Part3 = Voltage Sensor 25V
  Part4 = Current Sensor 5A
  Part5 = Jtron 1 Channel Optoisolated Relay Module [package=relay]
  BAT1 = 12 battery [package=battery]
  Mod1 = Solar Charge Controller [part_number="KLD Series Solar Charge Controller PWM" package=PWM-Model]
  Part6 = Solar Panel [package="Renogy 50 Watts 12 Volt Monocrystalline Bendable Solar Panel"]
  Part7 = Voltage Sensor 25V
  Mod2 = KY-018 Photoresistor Module [package="Breakout board"]
  Part8 = Jtron 1 Channel Optoisolated Relay Module [package=relay]

nets:
  N1: Part1.A0, Part4.2, Part4.OUT
  N2: Part1.A1, Part3.S
  N3: Part1.A2, Part7.S
  N4: Part1.D8, Part5.IN1
  N5: Part1.D2, Mod2.S
  N6: Part1.D7, Part8.IN1
  VCC: Part1.5V, Part4.VCC, Mod2.Vin, Part8.VCC
  GND: Part1.GND, Part3.-, Part4.GND, Part5.GND, Part7.+, Part7.-, Mod2.-, Part8.GND
  N7: BAT1.-, Mod1.Connector_4
  N8: BAT1.+, Mod1.Connector_3
  N9: Mod1.Connector_1, Part6.Connector_1
  N10: Mod1.Connector_2, Part6.Connector_2

custom parts:
  12 battery: 12V lead acid type battery, like the Husqvarna YTH2448 12V 35AH battery. This is the mini version 1/4 the size of the actual battery to be closer to typical breadboard parts (around 2in wide rathher than 7in). The pads in pcb are sized to accomidate up to 14ga wire (as these batterys will deliver high currents.)
  Solar Charge Controller: PWM-Solar Charge Controller
  Solar Panel: Renogy 50 Watts 12 Volt Solar Panel
  KY-018 Photoresistor Module: KY-018 Photoresistor module, used to measure light intensity. It can determine the presence or absence of light.
